# Fritzing sketch 1_24207623537 (saved by Fritzing 1.0.5)
breadboards: 1

parts:
  Part1 = Arduino Uno (Rev3)
  LED1 = smd LED [color="Red (633nm)" package="0805 [SMD]"]
  S1 = Pushbutton [package="[THT]"]
  R1 = Resistor [tolerance=±5% power=0.25W resistance=220 package=THT]

nets:
  N1: Part1.D13/SCK, R1.Pin_0
  N2: Part1.D2, S1.Pin_1, S1.Pin_2
  N3: Part1.GND, LED1.cathode, S1.Pin_3, S1.Pin_4
  N4: LED1.anode, R1.Pin_1
